// Logisim project Projeto.circ as structural Verilog
module \Dário  (
  input  in_1,
  input  in_2,
  input  [7:0] in_3,
  output [7:0] out_4
);

  wire and_1_out, and_2_out, and_3_out, and_4_out, and_5_out, and_6_out, and_7_out, and_8_out, and_9_out,
       and_10_out, and_11_out, and_12_out, and_13_out, and_14_out, and_15_out, and_16_out, and_17_out,
       and_18_out, and_19_out, and_20_out, and_21_out, and_22_out, and_23_out, and_24_out, and_25_out,
       and_26_out, and_27_out, and_31_out, and_32_out, and_33_out, and_34_out, and_35_out, and_36_out,
       and_37_out, and_38_out, and_39_out, not_1_out, not_2_out, not_3_out, not_4_out, not_5_out, not_6_out,
       not_7_out, not_8_out, not_9_out, not_10_out, not_11_out, not_12_out, not_13_out, not_14_out,
       not_15_out, not_16_out, pulso2, pulso4, pulso6, pulso8;

  not not_1 (not_1_out, out_4[0]);
  and and_1 (and_1_out, 1'b1, not_1_out);
  and and_2 (and_2_out, 1'b1, out_4[0]);
  and and_3 (and_3_out, in_3[0], in_2);
  not not_2 (not_2_out, in_3[0]);
  not not_3 (not_3_out, out_4[2]);
  and and_4 (and_4_out, pulso2, not_3_out);
  and and_5 (and_5_out, out_4[2], pulso2);
  and and_6 (and_6_out, in_3[2], in_2);
  not not_4 (not_4_out, in_3[2]);
  not not_5 (not_5_out, out_4[4]);
  and and_7 (and_7_out, pulso4, not_5_out);
  and and_8 (and_8_out, out_4[4], pulso4);
  and and_9 (and_9_out, in_3[4], in_2);
  not not_6 (not_6_out, in_3[4]);
  J_K_Flip_Flop j_k_ff_1 (
    .J(and_1_out), .clk(in_1), .K(and_2_out), .Q(out_4[0]), .preset(and_3_out), .reset(and_10_out));  // open: Qn, en
  and and_10 (and_10_out, not_2_out, in_2);
  J_K_Flip_Flop j_k_ff_2 (
    .J(and_4_out), .clk(in_1), .K(and_5_out), .Q(out_4[2]), .preset(and_6_out), .reset(and_11_out));  // open: Qn, en
  and and_11 (and_11_out, not_4_out, in_2);
  J_K_Flip_Flop j_k_ff_3 (
    .J(and_7_out), .clk(in_1), .K(and_8_out), .Q(out_4[4]), .preset(and_9_out), .reset(and_12_out));  // open: Qn, en
  and and_12 (and_12_out, not_6_out, in_2);
  and and_13 (and_13_out, 1'b1, out_4[0]);
  not not_7 (not_7_out, out_4[1]);
  and and_14 (and_14_out, and_13_out, not_7_out);
  and and_15 (and_15_out, out_4[1], and_13_out);
  and and_16 (and_16_out, pulso2, out_4[2]);
  not not_8 (not_8_out, out_4[3]);
  and and_17 (and_17_out, and_16_out, not_8_out);
  and and_18 (and_18_out, pulso4, out_4[4]);
  not not_9 (not_9_out, out_4[5]);
  and and_19 (and_19_out, and_18_out, not_9_out);
  J_K_Flip_Flop j_k_ff_4 (
    .J(and_14_out), .clk(in_1), .K(and_15_out), .Q(out_4[1]), .preset(and_20_out), .reset(and_21_out));  // open: Qn, en
  and and_20 (and_20_out, in_3[1], in_2);
  not not_10 (not_10_out, in_3[1]);
  and and_21 (and_21_out, not_10_out, in_2);
  and and_22 (and_22_out, out_4[3], and_16_out);
  J_K_Flip_Flop j_k_ff_5 (
    .J(and_17_out), .clk(in_1), .K(and_22_out), .Q(out_4[3]), .preset(and_23_out), .reset(and_24_out));  // open: Qn, en
  and and_23 (and_23_out, in_3[3], in_2);
  not not_11 (not_11_out, in_3[3]);
  and and_24 (and_24_out, not_11_out, in_2);
  and and_25 (and_25_out, out_4[5], and_18_out);
  J_K_Flip_Flop j_k_ff_6 (
    .J(and_19_out), .clk(in_1), .K(and_25_out), .Q(out_4[5]), .preset(and_26_out), .reset(and_27_out));  // open: Qn, en
  and and_26 (and_26_out, in_3[5], in_2);
  not not_12 (not_12_out, in_3[5]);
  and and_27 (and_27_out, not_12_out, in_2);
  and and_28 (pulso2, and_13_out, out_4[1]);
  and and_29 (pulso4, and_16_out, out_4[3]);
  and and_30 (pulso6, and_18_out, out_4[5]);
  not not_13 (not_13_out, out_4[6]);
  and and_31 (and_31_out, pulso6, not_13_out);
  and and_32 (and_32_out, out_4[6], pulso6);
  J_K_Flip_Flop j_k_ff_7 (
    .J(and_31_out), .clk(in_1), .K(and_32_out), .Q(out_4[6]), .preset(and_33_out), .reset(and_34_out));  // open: Qn, en
  and and_33 (and_33_out, in_3[6], in_2);
  not not_14 (not_14_out, in_3[6]);
  and and_34 (and_34_out, not_14_out, in_2);
  and and_35 (and_35_out, pulso6, out_4[6]);
  not not_15 (not_15_out, out_4[7]);
  and and_36 (and_36_out, and_35_out, not_15_out);
  and and_37 (and_37_out, out_4[7], and_35_out);
  J_K_Flip_Flop j_k_ff_8 (
    .J(and_36_out), .clk(in_1), .K(and_37_out), .Q(out_4[7]), .preset(and_38_out), .reset(and_39_out));  // open: Qn, en
  and and_38 (and_38_out, in_3[7], in_2);
  not not_16 (not_16_out, in_3[7]);
  and and_39 (and_39_out, not_16_out, in_2);
  and and_40 (pulso8, and_35_out, out_4[7]);

  // Other names for the same wires on the sheet: c = in_1; e1 = in_3[0]; e2 = in_3[1]; e3 = in_3[2]; e4 = in_3[3];
  //   e5 = in_3[4]; e6 = in_3[5]; e7 = in_3[6]; e8 = in_3[7]; s1 = out_4[0]; s2 = out_4[1]; s3 = out_4[2];
  //   s4 = out_4[3]; s5 = out_4[4]; s6 = out_4[5]; s7 = out_4[6]; s8 = out_4[7]; Setter = in_2
endmodule

module Controlador (
  input  in_1,
  input  [15:0] \Conteúdo_do_IR ,
  output Memory_out_in,
  output IR_out_in,
  output PC_plus_plus,
  output out_6,
  output out_7,
  output out_8,
  output out_9,
  output out_10
);

  wire and_2_out, and_3_out, and_6_out, and_7_out, and_8_out, est0, est1, est2, nand_1_out, NOP_out,
       not_1_out, not_2_out, not_3_out, not_4_out, not_5_out, not_6_out, not_7_out, not_8_out, not_9_out,
       not_10_out, not_11_out, not_12_out, not_13_out, not_14_out, not_15_out, not_16_out, not_17_out,
       not_18_out, not_19_out, not_20_out, not_21_out, not_22_out, not_23_out, not_24_out, not_25_out,
       not_26_out, not_27_out, not_28_out, not_29_out, not_30_out, s1, s2;

  not not_1 (not_1_out, s1);
  not not_2 (not_2_out, s2);
  and and_1 (est0, not_2_out, not_1_out);
  not not_3 (not_3_out, s1);
  and and_2 (and_2_out, 1'b1, not_3_out);
  and and_3 (and_3_out, 1'b1, s1);
  J_K_Flip_Flop j_k_ff_1 (.J(and_2_out), .clk(in_1), .K(and_3_out), .Q(s1));  // open: Qn, preset, en, reset
  and and_4 (est1, s1, not_2_out);
  and and_5 (est2, s2, not_1_out);
  and and_6 (and_6_out, 1'b1, s1);
  not not_4 (not_4_out, s2);
  and and_7 (and_7_out, and_6_out, not_4_out);
  and and_8 (and_8_out, s2, and_6_out);
  J_K_Flip_Flop j_k_ff_2 (.J(and_7_out), .clk(in_1), .K(and_8_out), .Q(s2));  // open: Qn, preset, en, reset
  and and_9 (out_6, s2, s1);
  not not_5 (not_5_out, \Conteúdo_do_IR [10]);
  not not_6 (not_6_out, \Conteúdo_do_IR [12]);
  not not_7 (not_7_out, \Conteúdo_do_IR [13]);
  not not_8 (not_8_out, \Conteúdo_do_IR [14]);
  not not_9 (not_9_out, \Conteúdo_do_IR [15]);
  not not_10 (not_10_out, \Conteúdo_do_IR [8]);
  not not_11 (not_11_out, \Conteúdo_do_IR [9]);
  not not_12 (not_12_out, \Conteúdo_do_IR [12]);
  not not_13 (not_13_out, \Conteúdo_do_IR [13]);
  not not_14 (not_14_out, \Conteúdo_do_IR [14]);
  not not_15 (not_15_out, \Conteúdo_do_IR [15]);
  and LDA (out_8, \Conteúdo_do_IR [8], \Conteúdo_do_IR [9], not_5_out, \Conteúdo_do_IR [11], not_6_out, not_7_out, not_8_out, not_9_out);
  and STA (out_10, not_10_out, not_11_out, \Conteúdo_do_IR [10], \Conteúdo_do_IR [11], not_12_out, not_13_out, not_14_out, not_15_out);
  not not_16 (not_16_out, est1);
  nand nand_1 (nand_1_out, est1, est0);
  or or_1 (IR_out_in, est0, not_16_out);
  not not_17 (not_17_out, \Conteúdo_do_IR [8]);
  not not_18 (not_18_out, \Conteúdo_do_IR [10]);
  not not_19 (not_19_out, \Conteúdo_do_IR [11]);
  not not_20 (not_20_out, \Conteúdo_do_IR [14]);
  not not_21 (not_21_out, \Conteúdo_do_IR [15]);
  and NOP (NOP_out, not_17_out, \Conteúdo_do_IR [9], not_18_out, not_19_out, \Conteúdo_do_IR [12], \Conteúdo_do_IR [13], not_20_out, not_21_out);
  xor xor_1 (Memory_out_in, nand_1_out, out_10);
  not not_22 (not_22_out, \Conteúdo_do_IR [8]);
  not not_23 (not_23_out, \Conteúdo_do_IR [11]);
  not not_24 (not_24_out, \Conteúdo_do_IR [12]);
  not not_25 (not_25_out, \Conteúdo_do_IR [13]);
  not not_26 (not_26_out, \Conteúdo_do_IR [15]);
  not not_27 (not_27_out, \Conteúdo_do_IR [10]);
  not not_28 (not_28_out, \Conteúdo_do_IR [11]);
  not not_29 (not_29_out, \Conteúdo_do_IR [14]);
  not not_30 (not_30_out, \Conteúdo_do_IR [15]);
  and JMP (out_7, \Conteúdo_do_IR [8], \Conteúdo_do_IR [9], not_27_out, not_28_out, \Conteúdo_do_IR [12], \Conteúdo_do_IR [13], not_29_out, not_30_out);
  and STP (out_9, not_22_out, \Conteúdo_do_IR [9], \Conteúdo_do_IR [10], not_23_out, not_24_out, not_25_out, \Conteúdo_do_IR [14], not_26_out);

  assign PC_plus_plus = out_6;

  // Other names for the same wires on the sheet: c = in_1; est3 = out_6; IR_In[15:0] = \Conteúdo_do_IR ; STA = out_10

  // Notes on the sheet:
  //   Estado 0
  //   Estado 1
  //   Estado 2
  //   Estado 3
endmodule

module Main (
);

  wire Clock, clock_1_out, controlador_1_ir_out_in, controlador_1_memory_out_in, controlador_1_out_7,
       controlador_1_pc_plus_plus, IRCLEAR, LDA, not_1_out, not_2_out, or_1_out, STA, STOP;
  wire [7:0] \dário_1_out_4 , Endereco, multiplexer_1_out, multiplexer_2_out;
  wire [15:0] ACC_q, controlled_buffer_1_out, controlled_buffer_3_out, ram_1_data;
  wire [15:8] IR_q;

  RAM #(.dataWidth(16)) ram_1 (
    .addr(multiplexer_2_out), .data(ram_1_data), .clk(Clock), .ld(controlador_1_memory_out_in));  // open: sel, clr
  assign controlled_buffer_1_out = LDA ? ram_1_data : 16'bz;  // Controlled_Buffer controlled_buffer_1
  Controlador controlador_1 (
    .Memory_out_in(controlador_1_memory_out_in), .IR_out_in(controlador_1_ir_out_in),
    .\Conteúdo_do_IR ({IR_q, Endereco}), .PC_plus_plus(controlador_1_pc_plus_plus), .in_1(Clock),
    .out_8(LDA), .out_7(controlador_1_out_7), .out_6(IRCLEAR), .out_9(STOP), .out_10(STA));
  Register #(.width(16)) ACC (.D(controlled_buffer_1_out), .Q(ACC_q), .clk(Clock));  // open: en, clr
  Multiplexer #(.width(8), .enable("false")) multiplexer_1 (
    .in0({8{1'b0}}), .in1(Endereco), .out(multiplexer_1_out), .sel(controlador_1_out_7));
  assign ram_1_data = STA ? ACC_q : 16'bz;  // Controlled_Buffer controlled_buffer_2
  Multiplexer #(.width(8), .enable("false")) multiplexer_2 (
    .in0(\dário_1_out_4 ), .in1(Endereco), .out(multiplexer_2_out), .sel(or_1_out));
  or or_1 (or_1_out, LDA, STA);
  \Dário  \dário_1  (
    .out_4(\dário_1_out_4 ), .in_1(controlador_1_pc_plus_plus), .in_3(multiplexer_1_out),
    .in_2(controlador_1_out_7));
  assign controlled_buffer_3_out = not_1_out ? ram_1_data : 16'bz;  // Controlled_Buffer controlled_buffer_3
  not not_1 (not_1_out, STA);
  Clock clock_1 (.out(clock_1_out));
  Register #(.width(16)) IR (
    .D(controlled_buffer_3_out), .Q({IR_q, Endereco}), .clk(controlador_1_ir_out_in), .clr(IRCLEAR));  // open: en
  not not_2 (not_2_out, STOP);
  and and_1 (Clock, clock_1_out, not_2_out);
endmodule

module IF (
  input  [15:0] \Conteúdo_do_IR 
);

  wire and_1_out, and_2_out, and_3_out, and_4_out, not_1_out, not_2_out, not_3_out, not_4_out, not_5_out,
       not_6_out, not_7_out, not_8_out, not_9_out, not_10_out, not_11_out, not_12_out, not_13_out,
       not_14_out, not_15_out, not_16_out, not_17_out, not_18_out, not_19_out, not_20_out, not_21_out;

  not not_1 (not_1_out, \Conteúdo_do_IR [10]);
  not not_2 (not_2_out, \Conteúdo_do_IR [12]);
  not not_3 (not_3_out, \Conteúdo_do_IR [13]);
  not not_4 (not_4_out, \Conteúdo_do_IR [14]);
  not not_5 (not_5_out, \Conteúdo_do_IR [15]);
  not not_6 (not_6_out, \Conteúdo_do_IR [8]);
  not not_7 (not_7_out, \Conteúdo_do_IR [9]);
  not not_8 (not_8_out, \Conteúdo_do_IR [12]);
  not not_9 (not_9_out, \Conteúdo_do_IR [13]);
  not not_10 (not_10_out, \Conteúdo_do_IR [14]);
  not not_11 (not_11_out, \Conteúdo_do_IR [15]);
  and and_1 (and_1_out, \Conteúdo_do_IR [8], \Conteúdo_do_IR [9], not_1_out, \Conteúdo_do_IR [11], not_2_out, not_3_out, not_4_out, not_5_out);
  and and_2 (and_2_out, not_6_out, not_7_out, \Conteúdo_do_IR [10], \Conteúdo_do_IR [11], not_8_out, not_9_out, not_10_out, not_11_out);
  not not_12 (not_12_out, \Conteúdo_do_IR [8]);
  not not_13 (not_13_out, \Conteúdo_do_IR [10]);
  not not_14 (not_14_out, \Conteúdo_do_IR [11]);
  not not_15 (not_15_out, \Conteúdo_do_IR [14]);
  not not_16 (not_16_out, \Conteúdo_do_IR [15]);
  not not_17 (not_17_out, \Conteúdo_do_IR [8]);
  not not_18 (not_18_out, \Conteúdo_do_IR [11]);
  not not_19 (not_19_out, \Conteúdo_do_IR [12]);
  not not_20 (not_20_out, \Conteúdo_do_IR [13]);
  not not_21 (not_21_out, \Conteúdo_do_IR [15]);
  and and_3 (and_3_out, not_12_out, \Conteúdo_do_IR [9], not_13_out, not_14_out, \Conteúdo_do_IR [12], \Conteúdo_do_IR [13], not_15_out, not_16_out);
  and and_4 (and_4_out, not_17_out, \Conteúdo_do_IR [9], \Conteúdo_do_IR [10], not_18_out, not_19_out, not_20_out, \Conteúdo_do_IR [14], not_21_out);

  // Other names for the same wires on the sheet: IR_In[15:0] = \Conteúdo_do_IR 
endmodule
